// Logisim project Ampelschaltung_v2_14(final).circ as structural Verilog: 4 circuits, main circuit main
module main (
);

  wire button_1_out, button_2_out, clock_1_out, not_1_out,
       \verkehr_grün_gelb_phase_fußgänger_rotphase_taster_1_gelbphase_verkehr ,
       \verkehr_grün_gelb_phase_fußgänger_rotphase_taster_1_signal_weiche ,
       \verkehr_rotgelb_phase_fußgänger_grünphase_1_gelbphase_verkehr ,
       \verkehr_rotgelb_phase_fußgänger_grünphase_1_signal_weiche , weiche_1_out_a, weiche_1_out_b;
  wire [2:0] or_2_out, \verkehr_rotgelb_phase_fußgänger_grünphase_1_rotphase_verkehr ;

  Weiche weiche_1 (
    .Out_b(weiche_1_out_b), .Out_a(weiche_1_out_a),
    .In(\verkehr_rotgelb_phase_fußgänger_grünphase_1_signal_weiche ), .clk(clock_1_out),
    .In_2(\verkehr_grün_gelb_phase_fußgänger_rotphase_taster_1_signal_weiche ));
  Clock clock_1 (.out(clock_1_out));
  \Verkehr_RotGelb_Phase___Fußgänger_Grünphase  \verkehr_rotgelb_phase_fußgänger_grünphase_1  (
    .clk(weiche_1_out_b), .Signal_Weiche(\verkehr_rotgelb_phase_fußgänger_grünphase_1_signal_weiche ),
    .Rotphase_Verkehr(\verkehr_rotgelb_phase_fußgänger_grünphase_1_rotphase_verkehr [0]),
    .Gelbphase_Verkehr(\verkehr_rotgelb_phase_fußgänger_grünphase_1_gelbphase_verkehr ),
    .\Grünphase_Fußgänger (or_2_out[0]));
  \Verkehr_Grün_Gelb_Phase___Fußgänger_Rotphase___Taster  \verkehr_grün_gelb_phase_fußgänger_rotphase_taster_1  (
    .\Grünphase_Verkehr (\verkehr_rotgelb_phase_fußgänger_grünphase_1_rotphase_verkehr [2]),
    .\Taster_Fußgänger (or_2_out[1]),
    .Gelbphase_Verkehr(\verkehr_grün_gelb_phase_fußgänger_rotphase_taster_1_gelbphase_verkehr ),
    .clk(weiche_1_out_a), .\Rotphase_Fußgänger (or_2_out[2]),
    .Signal_Weiche(\verkehr_grün_gelb_phase_fußgänger_rotphase_taster_1_signal_weiche ));
  or or_1 (\verkehr_rotgelb_phase_fußgänger_grünphase_1_rotphase_verkehr [1], \verkehr_rotgelb_phase_fußgänger_grünphase_1_gelbphase_verkehr , \verkehr_grün_gelb_phase_fußgänger_rotphase_taster_1_gelbphase_verkehr );
  or or_2 (or_2_out[1], button_2_out, button_1_out);
  LED led_1 (.in(or_2_out[2]));
  LED led_2 (.in(or_2_out[0]));
  Button button_1 (.out(button_1_out));
  DotMatrix #(.matrixcols(10), .matrixrows(31)) dotmatrix_1 (
    .col0({31{1'b1}}), .col1({31{1'b1}}), .col2({31{1'b1}}), .col3({31{1'b1}}), .col4({31{1'b1}}),
    .col5({31{1'b1}}), .col6({31{1'b1}}), .col7({31{1'b1}}), .col8({31{1'b1}}), .col9({31{1'b1}}));
  LED led_3 (.in(\verkehr_rotgelb_phase_fußgänger_grünphase_1_rotphase_verkehr [0]));
  LED led_4 (.in(\verkehr_rotgelb_phase_fußgänger_grünphase_1_rotphase_verkehr [1]));
  LED led_5 (.in(\verkehr_rotgelb_phase_fußgänger_grünphase_1_rotphase_verkehr [2]));
  DotMatrix #(.inputtype("row"), .matrixcols(1), .matrixrows(28)) dotmatrix_2 (
    .row0(not_1_out), .row1(not_1_out), .row2(not_1_out), .row3(1'b1), .row4(1'b1), .row5(not_1_out),
    .row6(not_1_out), .row7(not_1_out), .row8(1'b1), .row9(1'b1), .row10(not_1_out), .row11(not_1_out),
    .row12(not_1_out), .row13(1'b1), .row14(1'b1), .row15(not_1_out), .row16(not_1_out), .row17(not_1_out),
    .row18(1'b1), .row19(1'b1), .row20(not_1_out), .row21(not_1_out), .row22(not_1_out), .row23(1'b1),
    .row24(1'b1), .row25(not_1_out), .row26(not_1_out), .row27(not_1_out));
  Button button_2 (.out(button_2_out));
  LED led_6 (.in(or_2_out[2]));
  LED led_7 (.in(or_2_out[0]));
  not not_1 (not_1_out, 1'b1);
endmodule

module \Verkehr_RotGelb_Phase___Fußgänger_Grünphase  (
  input  clk,
  output Signal_Weiche,
  output Rotphase_Verkehr,
  output \Grünphase_Fußgänger ,
  output Gelbphase_Verkehr
);

  wire and_1_out, and_2_out, and_3_out, d_ff_1_q, d_ff_1_qn, d_ff_2_q, d_ff_2_qn, d_ff_3_q, d_ff_3_qn,
       d_ff_4_q, d_ff_4_qn, d_ff_5_q, d_ff_5_qn, d_ff_6_q, d_ff_6_qn, not_1_out, not_2_out, not_3_out,
       not_4_out, not_5_out, not_6_out;

  D_Flip_Flop d_ff_1 (
    .clk(clk), .D(d_ff_1_qn), .Q(d_ff_1_q), .Qn(d_ff_1_qn), .reset(Signal_Weiche));  // open: preset, en
  D_Flip_Flop d_ff_2 (
    .clk(d_ff_1_q), .D(d_ff_2_qn), .Q(d_ff_2_q), .Qn(d_ff_2_qn), .reset(Signal_Weiche));  // open: preset, en
  D_Flip_Flop d_ff_3 (
    .clk(d_ff_2_q), .D(d_ff_3_qn), .Q(d_ff_3_q), .Qn(d_ff_3_qn), .reset(Signal_Weiche));  // open: preset, en
  D_Flip_Flop d_ff_4 (
    .clk(d_ff_3_q), .D(d_ff_4_qn), .Q(d_ff_4_q), .Qn(d_ff_4_qn), .reset(Signal_Weiche));  // open: preset, en
  D_Flip_Flop d_ff_5 (
    .clk(d_ff_4_q), .D(d_ff_5_qn), .Q(d_ff_5_q), .Qn(d_ff_5_qn), .reset(Signal_Weiche));  // open: preset, en
  D_Flip_Flop d_ff_6 (
    .clk(d_ff_5_q), .D(d_ff_6_qn), .Q(d_ff_6_q), .Qn(d_ff_6_qn), .reset(Signal_Weiche));  // open: preset, en
  not not_1 (not_1_out, d_ff_1_q);
  not not_2 (not_2_out, d_ff_2_q);
  not not_3 (not_3_out, d_ff_3_q);
  not not_4 (not_4_out, d_ff_4_q);
  not not_5 (not_5_out, d_ff_5_q);
  not not_6 (not_6_out, d_ff_6_q);
  LED led_1 (.in(not_2_out));
  LED led_2 (.in(not_1_out));
  LED led_3 (.in(not_3_out));
  LED led_4 (.in(not_5_out));
  LED led_5 (.in(not_6_out));
  LED led_6 (.in(not_4_out));
  and and_1 (and_1_out, not_1_out, not_2_out, not_3_out, not_4_out, ~not_5_out, ~not_6_out);  // AND_Gate
  and and_2 (and_2_out, not_1_out, not_2_out, ~not_3_out, not_4_out, ~not_5_out, ~not_6_out);  // AND_Gate
  and and_3 (and_3_out, ~not_1_out, ~not_2_out, ~not_3_out, ~not_4_out, ~not_5_out, ~not_6_out);  // AND_Gate
  D_Flip_Flop #(.trigger("high")) d_ff_7 (.clk(clk), .D(and_1_out), .Q(Signal_Weiche));  // open: Qn, preset, en, reset
  S_R_Flip_Flop #(.trigger("high")) s_r_ff_1 (
    .S(and_3_out), .clk(clk), .R(and_1_out), .Q(\Grünphase_Fußgänger ));  // open: Qn, preset, reset, en
  S_R_Flip_Flop #(.trigger("high")) s_r_ff_2 (
    .S(and_2_out), .clk(clk), .R(and_1_out), .Q(Gelbphase_Verkehr));  // open: Qn, preset, reset, en

  assign Rotphase_Verkehr = \Grünphase_Fußgänger ;

  // Notes on the sheet:
  //   Timer Reset: 15s @ 2Hz
endmodule

module \Verkehr_Grün_Gelb_Phase___Fußgänger_Rotphase___Taster  (
  input  clk,
  input  \Taster_Fußgänger ,
  output Signal_Weiche,
  output \Grünphase_Verkehr ,
  output \Rotphase_Fußgänger ,
  output Gelbphase_Verkehr
);

  wire and_1_out, and_2_out, and_3_out, and_4_out, and_5_out, d_ff_1_q, d_ff_1_qn, d_ff_2_q, d_ff_2_qn,
       d_ff_3_q, d_ff_3_qn, d_ff_4_q, d_ff_4_qn, d_ff_5_q, d_ff_5_qn, d_ff_6_q, d_ff_6_qn, not_1_out,
       not_2_out, not_3_out, not_4_out, not_5_out, not_6_out, or_1_out, or_2_out, or_3_out, s_r_ff_3_q;
  wire [4:4] and_6_out;

  or or_1 (or_1_out, Signal_Weiche, and_6_out[4]);
  or or_2 (or_2_out, Signal_Weiche, and_6_out[4]);
  or or_3 (or_3_out, Signal_Weiche, and_6_out[4]);
  D_Flip_Flop d_ff_1 (.clk(clk), .D(d_ff_1_qn), .Q(d_ff_1_q), .Qn(d_ff_1_qn), .reset(or_1_out));  // open: preset, en
  D_Flip_Flop d_ff_2 (
    .clk(d_ff_1_q), .D(d_ff_2_qn), .Q(d_ff_2_q), .Qn(d_ff_2_qn), .reset(or_2_out));  // open: preset, en
  D_Flip_Flop d_ff_3 (
    .clk(d_ff_2_q), .D(d_ff_3_qn), .Q(d_ff_3_q), .Qn(d_ff_3_qn), .preset(and_6_out[4]), .reset(Signal_Weiche));  // open: en
  D_Flip_Flop d_ff_4 (
    .clk(d_ff_3_q), .D(d_ff_4_qn), .Q(d_ff_4_q), .Qn(d_ff_4_qn), .preset(and_6_out[4]), .reset(Signal_Weiche));  // open: en
  D_Flip_Flop d_ff_5 (
    .clk(d_ff_4_q), .D(d_ff_5_qn), .Q(d_ff_5_q), .Qn(d_ff_5_qn), .reset(or_3_out));  // open: preset, en
  D_Flip_Flop d_ff_6 (
    .clk(d_ff_5_q), .D(d_ff_6_qn), .Q(d_ff_6_q), .Qn(d_ff_6_qn), .reset(Signal_Weiche));  // open: preset, en
  not not_1 (not_1_out, d_ff_1_q);
  not not_2 (not_2_out, d_ff_2_q);
  not not_3 (not_3_out, d_ff_3_q);
  not not_4 (not_4_out, d_ff_4_q);
  not not_5 (not_5_out, d_ff_5_q);
  not not_6 (not_6_out, d_ff_6_q);
  LED led_1 (.in(not_1_out));
  LED led_2 (.in(not_2_out));
  LED led_3 (.in(not_4_out));
  LED led_4 (.in(not_5_out));
  LED led_5 (.in(not_3_out));
  LED led_6 (.in(not_6_out));
  and and_1 (and_1_out, ~not_1_out, not_2_out, not_3_out, not_4_out, not_5_out, ~not_6_out);  // AND_Gate
  and and_2 (and_2_out, ~not_1_out, not_2_out, ~not_3_out, not_4_out, not_5_out, ~not_6_out);  // AND_Gate
  and and_3 (and_3_out, ~not_1_out, ~not_2_out, ~not_3_out, ~not_4_out, ~not_5_out, ~not_6_out);  // AND_Gate
  and and_4 (and_4_out, ~not_1_out, not_2_out, not_4_out, not_4_out, ~not_5_out, ~not_6_out);  // AND_Gate
  and and_5 (and_5_out, not_1_out, ~not_2_out, ~not_4_out, ~not_4_out, ~not_5_out, ~not_6_out);  // AND_Gate
  D_Flip_Flop #(.trigger("high")) d_ff_7 (.clk(clk), .D(and_1_out), .Q(Signal_Weiche));  // open: Qn, preset, en, reset
  S_R_Flip_Flop #(.trigger("high")) s_r_ff_1 (
    .S(and_3_out), .clk(clk), .R(and_1_out), .Q(\Grünphase_Verkehr ));  // open: Qn, preset, reset, en
  S_R_Flip_Flop #(.trigger("high")) s_r_ff_2 (
    .S(and_2_out), .clk(clk), .R(and_1_out), .Q(Gelbphase_Verkehr));  // open: Qn, preset, reset, en
  S_R_Flip_Flop #(.trigger("high")) s_r_ff_3 (
    .S(and_5_out), .clk(clk), .R(and_4_out), .Q(s_r_ff_3_q));  // open: Qn, preset, reset, en
  and and_6 (and_6_out[4], s_r_ff_3_q, \Taster_Fußgänger );

  assign \Rotphase_Fußgänger  = \Grünphase_Verkehr ;

  // Notes on the sheet:
  //   Timer Reset: 15s @ 2Hz
  //   Skip to 20s @ 2Hz
endmodule

module Weiche (
  input  In,
  input  clk,
  input  In_2,
  output Out_a,
  output Out_b
);

  wire j_k_ff_1_q, j_k_ff_1_qn, or_1_out;

  J_K_Flip_Flop j_k_ff_1 (
    .J(or_1_out), .clk(or_1_out), .K(or_1_out), .Q(j_k_ff_1_q), .Qn(j_k_ff_1_qn));  // open: preset, en, reset
  or or_1 (or_1_out, In, In_2);
  and and_1 (Out_a, j_k_ff_1_qn, clk);
  and and_2 (Out_b, clk, j_k_ff_1_q);
endmodule
